# Fritzing sketch garage_door (saved by Fritzing 0.9.3b)
stripboards: 1

parts:
  M3 = DOIT Esp32 DevKit v1 (30 pins long, 11 pins width) [part_number=ESP32S-PIN30]  # not connected
  R34 = Resistor [tolerance=±5% resistance=10k package=THT]
  R35 = Resistor [tolerance=±5% resistance=10k package=THT]
  R36 = Resistor [tolerance=±5% resistance=10k package=THT]
  J34 = female pin header, 6 pins [form="♀ (female)"]
  J35 = female pin header, 6 pins [form="♀ (female)"]
  U13 = 4N25 [package=THT]
  U14 = 4N25 [package=THT]
  R37 = Resistor [tolerance=±5% resistance=220 package=THT]
  R38 = Resistor [tolerance=±5% resistance=220 package=THT]
  J36 = male pin header, 3 pins [form="♂ (male)"]
  J37 = male pin header, 3 pins [form="♂ (male)"]
  J38 = male pin header, 4 pins [form="♂ (male)"]
  R39 = Resistor [tolerance=±5% resistance=10k package=THT]
  J32 = female pin header, 2 pins [form="♀ (female)"]  # not connected
  J33 = female pin header, 2 pins [form="♀ (female)"]

nets:
  N1: R34.Pin_0, J36.pin2, J37.pin2, R39.Pin_0, J33.pin1
  N2: R34.Pin_1, R38.Pin_0, J36.pin3
  N3: R35.Pin_0, R36.Pin_0, J35.pin5, U13.Pin_2, U14.Pin_2, J36.pin1, J37.pin1, J38.pin2
  N4: R35.Pin_1, J35.pin1, U14.Pin_4
  N5: R36.Pin_1, J34.pin6, U13.Pin_4
  N6: J34.pin1, J38.pin3
  N7: J34.pin4, J38.pin4
  N8: J35.pin6, U13.Pin_5, U14.Pin_5, J38.pin1
  N9: U13.Pin_1, R37.Pin_1
  N10: U14.Pin_1, R38.Pin_1
  N11: R37.Pin_0, J37.pin3, R39.Pin_1

custom parts:
  DOIT Esp32 DevKit v1 (30 pins long, 11 pins width): The DOIT Esp32 DevKit v1 is one of the development board created by DOIT to evaluate the ESP-WROOM-32 module. It is based on the ESP32 microcontroller that boasts Wifi, Bluetooth, Ethernet and Low Power support all in a single chip. (vanepp) made breadboard work, adjusted pin numbering and labels and reduced size of schematic and cleaned up pcb. This chip is 30pins long (2 x15) and 11 pins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
  4N25: Optocoupler
